# Fritzing sketch chess_clock_v1 (saved by Fritzing 0.9.9b)
breadboards: 1

parts:
  Part1 = Arduino Uno (Rev3)
  RE1 = Rotary Encoder [package=THT]
  S1 = Pushbutton [package="[THT]"]
  LED1 = LED - 5mm [color="Red (633nm)" current=0.030 package="5 mm [THT]"]
  R1 = Resistor [tolerance=±5% resistance=220 package="0603 [SMD]"]
  S2 = Square Pushbutton
  Mod1 = Passive Buzzer
  J1 = Basic Servo

nets:
  N1: Part1.D1/TX, S2.leg1
  N2: Part1.D2, S1.Pin_1, S1.Pin_2
  N3: Part1.D3_PWM, RE1.EncoderPinC
  N4: Part1.D6_PWM, J1.pulse
  5V: Part1.5V, RE1.EncoderPinA, S1.Pin_3, S1.Pin_4, R1.Pin_1, S2.leg0, Mod1.-, J1.vcc
  GND: Part1.GND, RE1.EncoderPinB, LED1.anode, Mod1.S, J1.gnd
  N5: LED1.cathode, R1.Pin_0

notes:
  the encoder and button are one unit
